// Logisim project LC3-2200a.circ as structural Verilog: 2 circuits, main circuit my circuit
module my_circuit (
  input  in_1
);

  wire and_3_out, and_4_out, and_5_out, and_6_out, and_7_out, and_8_out, and_9_out, and_10_out, and_11_out,
       and_12_out, and_13_out, and_14_out, and_15_out, and_16_out, and_17_out, and_18_out, CLK,
       decoder_1_out0, decoder_1_out1, decoder_1_out2, decoder_1_out3, decoder_1_out4, decoder_1_out5,
       decoder_1_out6, decoder_1_out7, decoder_1_out8, decoder_1_out9, decoder_1_out10, decoder_1_out11,
       decoder_1_out12, decoder_1_out13, decoder_1_out14, decoder_1_out15, DrMEM, DrReg, LdIR, not_2_out,
       undriven, undriven_2, undriven_4, undriven_5, undriven_6, undriven_7, undriven_8, undriven_9,
       undriven_10, undriven_11, undriven_12, undriven_13, undriven_14, undriven_15, undriven_16,
       undriven_17, undriven_18, undriven_19, WrMEM;
  wire [1:0] func;
  wire [3:0] RegNo;
  wire [23:0] bit_extender_1_out, MAR_q;
  wire [31:0] adder_1_out, and_1_out, and_2_out, controlled_buffer_1_out, controlled_buffer_3_out, IR_q,
       multiplexer_1_out, multiplexer_2_out, not_1_out, PC_q, ram_1_data, register_1_q, register_2_q,
       register_3_q, register_4_q, register_5_q, register_6_q, register_7_q, register_8_q, register_9_q,
       register_10_q, register_11_q, register_12_q, register_13_q, register_14_q, register_15_q,
       register_16_q, register_17_q, register_18_q, shift, undriven_3;

  Register #(.width(32)) PC (.D(undriven_3), .Q(PC_q));  // open: en, clk, clr
  Controlled_Buffer #(.width(32)) controlled_buffer_1 (.in(PC_q), .out(controlled_buffer_1_out));  // open: en
  assign and_1_out = register_1_q & register_2_q;  // AND_Gate and_1, 32 bits wide
  assign and_2_out = register_1_q & register_2_q;  // AND_Gate and_2, 32 bits wide
  assign not_1_out = ~and_2_out;  // NOT_Gate not_1, 32 bits wide
  Multiplexer #(.select(2), .width(32), .disabled(0), .enable("false")) multiplexer_1 (
    .in0(and_1_out), .in1(not_1_out), .in2(adder_1_out), .in3(shift), .out(multiplexer_1_out), .sel(func));
  Controlled_Buffer #(.width(32)) controlled_buffer_2 (
    .in(multiplexer_1_out), .out(controlled_buffer_1_out));  // open: en
  Register #(.width(32)) register_1 (.D(undriven_3), .en(undriven), .Q(register_1_q));  // open: clk, clr
  Register #(.width(32)) register_2 (.D(undriven_3), .en(undriven_2), .Q(register_2_q));  // open: clk, clr
  Adder #(.width(32)) adder_1 (.a(register_1_q), .b(32'h1), .out(adder_1_out));  // open: cin, cout
  Decoder #(.select(4), .enable("false")) decoder_1 (
    .out0(decoder_1_out0), .out1(decoder_1_out1), .out2(decoder_1_out2), .out3(decoder_1_out3),
    .out4(decoder_1_out4), .out5(decoder_1_out5), .out6(decoder_1_out6), .out7(decoder_1_out7),
    .out8(decoder_1_out8), .out9(decoder_1_out9), .out10(decoder_1_out10), .out11(decoder_1_out11),
    .out12(decoder_1_out12), .out13(decoder_1_out13), .out14(decoder_1_out14), .out15(decoder_1_out15),
    .sel(RegNo));
  and and_3 (and_3_out, decoder_1_out0, in_1);
  and and_4 (and_4_out, decoder_1_out1, in_1);
  and and_5 (and_5_out, decoder_1_out2, in_1);
  and and_6 (and_6_out, decoder_1_out3, in_1);
  and and_7 (and_7_out, decoder_1_out4, in_1);
  and and_8 (and_8_out, decoder_1_out5, in_1);
  and and_9 (and_9_out, decoder_1_out6, in_1);
  and and_10 (and_10_out, decoder_1_out7, in_1);
  and and_11 (and_11_out, decoder_1_out8, in_1);
  and and_12 (and_12_out, decoder_1_out9, in_1);
  and and_13 (and_13_out, decoder_1_out10, in_1);
  and and_14 (and_14_out, decoder_1_out11, in_1);
  and and_15 (and_15_out, decoder_1_out12, in_1);
  and and_16 (and_16_out, decoder_1_out13, in_1);
  and and_17 (and_17_out, decoder_1_out14, in_1);
  and and_18 (and_18_out, decoder_1_out15, in_1);
  Register #(.width(32)) register_3 (.D(undriven_3), .en(and_3_out), .Q(register_3_q), .clk(CLK), .clr(undriven_4));
  Register #(.width(32)) register_4 (.D(undriven_3), .en(and_4_out), .Q(register_4_q), .clk(CLK), .clr(undriven_5));
  Register #(.width(32)) register_5 (.D(undriven_3), .en(and_5_out), .Q(register_5_q), .clk(CLK), .clr(undriven_6));
  Register #(.width(32)) register_6 (.D(undriven_3), .en(and_6_out), .Q(register_6_q), .clk(CLK), .clr(undriven_7));
  Register #(.width(32)) register_7 (.D(undriven_3), .en(and_7_out), .Q(register_7_q), .clk(CLK), .clr(undriven_8));
  Register #(.width(32)) register_8 (.D(undriven_3), .en(and_8_out), .Q(register_8_q), .clk(CLK), .clr(undriven_9));
  Register #(.width(32)) register_9 (.D(undriven_3), .en(and_9_out), .Q(register_9_q), .clk(CLK), .clr(undriven_10));
  Register #(.width(32)) register_10 (.D(undriven_3), .en(and_10_out), .Q(register_10_q), .clk(CLK), .clr(undriven_11));
  Register #(.width(32)) register_11 (.D(undriven_3), .en(and_11_out), .Q(register_11_q), .clk(CLK), .clr(undriven_12));
  Register #(.width(32)) register_12 (.D(undriven_3), .en(and_12_out), .Q(register_12_q), .clk(CLK), .clr(undriven_13));
  Register #(.width(32)) register_13 (.D(undriven_3), .en(and_13_out), .Q(register_13_q), .clk(CLK), .clr(undriven_14));
  Register #(.width(32)) register_14 (.D(undriven_3), .en(and_14_out), .Q(register_14_q), .clk(CLK), .clr(undriven_15));
  Register #(.width(32)) register_15 (.D(undriven_3), .en(and_15_out), .Q(register_15_q), .clk(CLK), .clr(undriven_16));
  Register #(.width(32)) register_16 (.D(undriven_3), .en(and_16_out), .Q(register_16_q), .clk(CLK), .clr(undriven_17));
  Register #(.width(32)) register_17 (.D(undriven_3), .en(and_17_out), .Q(register_17_q), .clk(CLK), .clr(undriven_18));
  Register #(.width(32)) register_18 (.D(undriven_3), .en(and_18_out), .Q(register_18_q), .clk(CLK), .clr(undriven_19));
  Multiplexer #(.select(4), .width(32), .disabled(0), .enable("false")) multiplexer_2 (
    .in0(register_3_q), .in1(register_4_q), .in2(register_5_q), .in3(register_6_q), .in4(register_7_q),
    .in5(register_8_q), .in6(register_9_q), .in7(register_10_q), .in8(register_11_q), .in9(register_12_q),
    .in10(register_13_q), .in11(register_14_q), .in12(register_15_q), .in13(register_16_q),
    .in14(register_17_q), .in15(register_18_q), .out(multiplexer_2_out), .sel(RegNo));
  assign controlled_buffer_3_out = DrReg ? multiplexer_2_out : 32'bz;  // Controlled_Buffer controlled_buffer_3
  Bit_Extender #(.in_width(32), .out_width(24)) bit_extender_1 (.in(undriven_3), .out(bit_extender_1_out));
  Register #(.width(24)) MAR (.D(bit_extender_1_out), .Q(MAR_q));  // open: en, clk, clr
  RAM #(.addrWidth(24), .dataWidth(32), .bus("separate")) ram_1 (
    .addr(MAR_q), .din(undriven_3), .data(ram_1_data), .clk(CLK), .ld(not_2_out));  // open: str, sel, clr
  not not_2 (not_2_out, WrMEM);
  assign controlled_buffer_3_out = DrMEM ? ram_1_data : 32'bz;  // Controlled_Buffer controlled_buffer_4
  Register #(.width(32)) IR (.D(undriven_3), .en(LdIR), .Q(IR_q));  // open: clk, clr
  ROM #(.addrWidth(24), .dataWidth(32)) rom_1 ();  // open: addr, data, sel
  ROM rom_2 ();  // open: addr, data, sel
  ROM rom_3 ();  // open: addr, data, sel

  // Other names for the same wires on the sheet: WrReg = in_1

  // Notes on the sheet:
  //   $zero
  //   $at
  //   $v0
  //   $a1
  //   $a2
  //   $t0
  //   $t1
  //   $t2
  //   $s1
  //   $s2
  //   $k0
  //   $sp
  //   $fp
  //   $ra
endmodule

module Registers (
);

  wire undriven, undriven_2, undriven_3, undriven_4, undriven_5, undriven_6, undriven_12, undriven_24,
       undriven_25, undriven_26, undriven_27, undriven_28, undriven_29, undriven_30;
  wire [7:0] register_1_q, register_2_q, register_3_q, register_4_q, register_5_q, register_6_q,
       register_7_q, register_8_q, register_9_q, register_10_q, register_11_q, register_12_q, register_13_q,
       register_14_q, register_15_q, register_16_q, undriven_7, undriven_8, undriven_9, undriven_10,
       undriven_11, undriven_13, undriven_14, undriven_15, undriven_16, undriven_17, undriven_18,
       undriven_19, undriven_20, undriven_21, undriven_22, undriven_23;

  Register register_1 (.D(undriven_7), .en(undriven), .Q(register_1_q), .clk(undriven_24), .clr(undriven_26));
  Register register_2 (.D(undriven_8), .en(undriven_2), .Q(register_2_q), .clk(undriven_25), .clr(undriven_27));
  Register register_3 (.D(undriven_9), .en(undriven_3), .Q(register_3_q), .clr(undriven_28));  // open: clk
  Register register_4 (.D(undriven_10), .en(undriven_4), .Q(register_4_q), .clk(undriven_6), .clr(undriven_29));
  Register register_5 (.D(undriven_11), .en(undriven_5), .Q(register_5_q), .clk(undriven_12), .clr(undriven_30));
  Register register_6 (.D(undriven_13), .Q(register_6_q));  // open: en, clk, clr
  Register register_7 (.D(undriven_14), .Q(register_7_q));  // open: en, clk, clr
  Register register_8 (.D(undriven_15), .Q(register_8_q));  // open: en, clk, clr
  Register register_9 (.D(undriven_16), .Q(register_9_q));  // open: en, clk, clr
  Register register_10 (.D(undriven_17), .Q(register_10_q));  // open: en, clk, clr
  Register register_11 (.D(undriven_18), .Q(register_11_q));  // open: en, clk, clr
  Register register_12 (.D(undriven_19), .Q(register_12_q));  // open: en, clk, clr
  Register register_13 (.D(undriven_20), .Q(register_13_q));  // open: en, clk, clr
  Register register_14 (.D(undriven_21), .Q(register_14_q));  // open: en, clk, clr
  Register register_15 (.D(undriven_22), .Q(register_15_q));  // open: en, clk, clr
  Register register_16 (.D(undriven_23), .Q(register_16_q));  // open: en, clk, clr

  // Notes on the sheet:
  //   $zero
  //   $at
  //   $v0
  //   $a0
  //   $a1
  //   $a2
  //   $t0
  //   $t1
  //   $t2
  //   $s0
  //   $s1
  //   $s2
  //   $k0
  //   $sp
  //   $fp
  //   $ra
endmodule
